# Fritzing sketch 회로도 (saved by Fritzing 0.9.3b)

parts:
  부품1 = Arduino Nano (Rev3.0)
  LED1 = smd LED [color="Red (633nm)" package="1206 [SMD]"]
  R1 = Resistor [tolerance=±5% resistance=220 package=THT]
  J1 = Piezo Speaker
  부품2 = MQ-7 breakout
  U1 = SWITCH-SPST-2 [package=r_sw_th]
  VCC1 = Battery block 9V

nets:
  N1: 부품1.D2, J1.pin2
  N2: 부품1.D3, LED1.anode
  N3: 부품1.VIN, U1.P
  N4: 부품1.GND, R1.Pin_1, J1.pin1, VCC1.-
  5V: 부품1.5V, 부품2.VCC
  N5: 부품1.A5, 부품2.AO

custom parts:
  MQ-7 breakout: SKU: 101282
