# Fritzing sketch Sketch (saved by Fritzing 0.9.3b)

parts:
  부품1 = Arduino Uno (Rev3)
  부품2 = Black Joystick KY-023

nets:
  N1: 부품1.A0, 부품2.VRx
  N2: 부품1.A1, 부품2.VRy
  N3: 부품1.D3_PWM, 부품2.SW
  5V: 부품1.5V, 부품2.+5V
  GND: 부품1.GND, 부품2.GND

custom parts:
  Black Joystick KY-023: Description: The joystick is a combination of 2 analoog potentiometer and a digital switch. Arduino GND --> Module pin - Arduino +5V --> Module pin +5V Arduino Analoog 0 --> Module VRx Arduino Analoog 1 --> Module VRy Arduino Digital --> Module SW Dimensions: 1" x 1.25"
