# Fritzing sketch Untitled Sketch (saved by Fritzing 0.9.3b)
circuit board: 8.46667cm x 5.64444cm

parts:
  부품1 = Arduino Uno (Rev3)
  Disp1 = LBT2088AH [part_number=LBT2088AH]

nets:
  N1: 부품1.A2, Disp1.pin_12
  N2: 부품1.A3, Disp1.pin_11
  N3: 부품1.A4/SDA, Disp1.pin_10
  N4: 부품1.A5/SCL, Disp1.pin_9
  N5: 부품1.D8, Disp1.pin_3
  N6: 부품1.D9_PWM, Disp1.pin_4
  N7: 부품1.D10_PWM/SS, Disp1.pin_5
  N8: 부품1.D11_PWM/MOSI, Disp1.pin_6
  N9: 부품1.D12/MISO, Disp1.pin_7
  N10: 부품1.D13/SCK, Disp1.pin_8
  N11: 부품1.D2, Disp1.pin_13
  N12: 부품1.D3_PWM, Disp1.pin_14
  N13: 부품1.D4, Disp1.pin_15
  N14: 부품1.D5_PWM, Disp1.pin_16
  N15: 부품1.D6_PWM, Disp1.pin1
  N16: 부품1.D7, Disp1.pin2
