# Fritzing sketch 회로 (saved by Fritzing 0.9.3b)

parts:
  부품1 = Arduino Uno (Rev3) - ICSP
  R1 = Resistor [tolerance=±5% resistance=220 package=THT]
  R2 = Resistor [tolerance=±5% resistance=220 package=THT]
  R3 = Resistor [tolerance=±5% resistance=220 package=THT]
  R4 = Resistor [tolerance=±5% resistance=220 package=THT]
  R5 = Resistor [tolerance=±5% resistance=220 package=THT]
  R6 = Resistor [tolerance=±5% resistance=220 package=THT]
  R7 = Resistor [tolerance=±5% resistance=220 package=THT]
  R8 = Resistor [tolerance=±5% resistance=220 package=THT]
  LED1 = LED - 5mm [color="Red (633nm)" package="5 mm [THT]"]
  LED2 = LED - 5mm [color="Red (633nm)" package="5 mm [THT]"]
  LED3 = LED - 5mm [color="Red (633nm)" package="5 mm [THT]"]
  LED4 = LED - 5mm [color="Red (633nm)" package="5 mm [THT]"]
  LED5 = LED - 5mm [color="Red (633nm)" package="5 mm [THT]"]
  LED6 = LED - 5mm [color="Red (633nm)" package="5 mm [THT]"]
  LED7 = LED - 5mm [color="Red (633nm)" package="5 mm [THT]"]
  LED8 = LED - 5mm [color="Red (633nm)" package="5 mm [THT]"]

nets:
  N1: 부품1.D8, R2.Pin_1
  N2: 부품1.D9_PWM, R1.Pin_1
  N3: 부품1.GND, LED5.cathode
  N4: 부품1.D2, R4.Pin_1
  N5: 부품1.D3_PWM, R5.Pin_1
  N6: 부품1.D4, R6.Pin_1
  N7: 부품1.D5_PWM, R7.Pin_1
  N8: 부품1.D6_PWM, R3.Pin_1
  N9: 부품1.D7, R8.Pin_1
  N10: R1.Pin_0, LED4.anode
  N11: R2.Pin_0, LED3.anode
  N12: R3.Pin_0, LED1.anode
  N13: R4.Pin_0, LED5.anode
  N14: R5.Pin_0, LED6.anode
  N15: R6.Pin_0, LED7.anode
  N16: R7.Pin_0, LED8.anode
  N17: R8.Pin_0, LED2.anode
