# Fritzing sketch 회로도 (saved by Fritzing 0.9.3b)
breadboards: 1

parts:
  부품1 = Arduino Uno (Rev3) - ICSP
  LED1 = smd LED [color="Red (633nm)" package="0805 [SMD]"]
  LED2 = smd LED [color="Red (633nm)" package="0805 [SMD]"]
  LED3 = smd LED [color="Red (633nm)" package="0805 [SMD]"]
  R1 = PHOTOCELL [package=photocell]
  R2 = Resistor [tolerance=±5% resistance=220 package=THT]
  R3 = Resistor [tolerance=±5% resistance=220 package=THT]
  R4 = Resistor [tolerance=±5% resistance=220 package=THT]
  R5 = Resistor [tolerance=±5% resistance=220 package=THT]

nets:
  N1: 부품1.A0, R1.P$1, R3.Pin_1
  N2: 부품1.D8, R2.Pin_1
  N3: 부품1.D9_PWM, R4.Pin_1
  N4: 부품1.D10_PWM/SS, R5.Pin_1
  N5: 부품1.5V, R1.P$2
  N6: 부품1.GND, LED1.cathode, LED2.cathode, LED3.cathode, R3.Pin_0
  N7: LED1.anode, R2.Pin_0
  N8: LED2.anode, R4.Pin_0
  N9: LED3.anode, R5.Pin_0
